// Logisim project Uebung_1.circ as structural Verilog: 1 circuit, main circuit main
module main (
  input  Schalter_Oben,
  input  Schalter_Heben,
  input  Schalter_Senken,
  input  Lichtschranke,
  input  Schalter_Unten,
  input  in_6,
  input  in_7
);

  wire and_1_out, and_2_out, and_3_out, d_ff_1_q, d_ff_2_q, d_ff_3_q, not_1_out, not_2_out, not_3_out;

  not not_1 (not_1_out, Schalter_Oben);
  not not_2 (not_2_out, Lichtschranke);
  not not_3 (not_3_out, Schalter_Unten);
  and and_1 (and_1_out, not_1_out, Schalter_Heben);
  and and_2 (and_2_out, Schalter_Senken, not_2_out);
  D_Flip_Flop d_ff_1 (.D(in_6), .clk(in_7), .Q(d_ff_1_q));  // open: Qn, preset, reset
  and and_3 (and_3_out, and_2_out, not_3_out);
  LED led_1 (.in(d_ff_1_q));
  D_Flip_Flop d_ff_2 (.D(d_ff_1_q), .clk(in_7), .Q(d_ff_2_q));  // open: Qn, preset, reset
  LED led_2 (.in(d_ff_2_q));
  D_Flip_Flop d_ff_3 (.D(d_ff_2_q), .clk(in_7), .Q(d_ff_3_q));  // open: Qn, preset, reset
  LED Motor_Heben (.in(and_1_out));
  LED Motor_Senken (.in(and_3_out));
  LED led_3 (.in(d_ff_3_q));
  D_Flip_Flop d_ff_4 (.D(d_ff_3_q), .clk(in_7));  // open: Q, Qn, preset, reset
endmodule
